// Logisim project PBPU2.circ as structural Verilog: 1 circuit, main circuit main
module main (
  input  in_1
);

  wire adder_1_cout, Carry_q, CLK, CycleCounter_carry, demultiplexer_1_out1, demultiplexer_1_out2,
       demultiplexer_1_out6, or_1_out;
  wire [1:0] CycleCount_data;
  wire [3:0] A_q, adder_1_out, B_q, controlled_buffer_1_out, controlled_buffer_2_out, InstructionReg_q,
       MEMORYBUS;
  wire [11:0] MemoryCounter_q;

  Counter #(.max('hfff), .width(12)) MemoryCounter (
    .clk(CLK), .Q(MemoryCounter_q));  // open: clr, load, up, count, D, carry
  Register #(.width(4)) InstructionReg (
    .D(MEMORYBUS), .en(CycleCounter_carry), .clk(CLK), .Q(InstructionReg_q));  // open: clr
  ROM #(.addrWidth(12), .dataWidth(4)) rom_1 (.addr(MemoryCounter_q), .data(MEMORYBUS));
  Demultiplexer #(.enable("false"), .select(4)) demultiplexer_1 (
    .out1(demultiplexer_1_out1), .out2(demultiplexer_1_out2), .out6(demultiplexer_1_out6),
    .in(CycleCounter_carry), .sel(InstructionReg_q));  // open: out0, out3, out4, out5, out7, out8, out9, out10, out11, out12, out13, out14, out15
  ROM #(.addrWidth(4), .dataWidth(2)) CycleCount (.addr(InstructionReg_q), .data(CycleCount_data));
  Clock clock_1 (.out(CLK));
  assign controlled_buffer_1_out = in_1 ? MEMORYBUS : 4'bz;  // Controlled_Buffer controlled_buffer_1
  Register #(.trigger("falling"), .width(4)) A (
    .D(controlled_buffer_2_out), .en(or_1_out), .clk(CLK), .Q(A_q));  // open: clr
  assign controlled_buffer_2_out = or_1_out ? controlled_buffer_1_out : 4'bz;  // Controlled_Buffer controlled_buffer_2
  or or_1 (or_1_out, demultiplexer_1_out1, demultiplexer_1_out6);
  Register #(.trigger("falling"), .width(4)) B (
    .D(MEMORYBUS), .en(demultiplexer_1_out2), .clk(CLK), .Q(B_q));  // open: clr
  Register #(.trigger("falling"), .width(1)) Carry (
    .D(adder_1_cout), .en(demultiplexer_1_out1), .clk(CLK), .Q(Carry_q));  // open: clr
  Counter #(.max('h3), .trigger("falling"), .width(2)) CycleCounter (
    .load(CycleCounter_carry), .up(1'b0), .clk(CLK), .D(CycleCount_data), .carry(CycleCounter_carry));  // open: clr, count, Q
  assign controlled_buffer_1_out = demultiplexer_1_out6 ? adder_1_out : 4'bz;  // Controlled_Buffer controlled_buffer_3
  Adder #(.width(4)) adder_1 (.a(A_q), .b(B_q), .out(adder_1_out), .cin(Carry_q), .cout(adder_1_cout));

  // Notes on the sheet:
  //   contents of rom_1 (hex, n*v repeats v):
  //   1 5 2 5 6
  //   contents of CycleCount (hex, n*v repeats v):
  //   0 1 1 2 2 8*0 2 2 2
endmodule
